# Fritzing sketch Catapulta_servo_motor (saved by Fritzing 0.8.3b)
breadboards: 1

parts:
  Part1 = Arduino Uno (Rev3)
  J1 = Basic Servo

nets:
  GND: Part1.GND, J1.gnd
  N1: Part1.D6_PWM, J1.pulse
  5V: Part1.5V, J1.vcc
